// Logisim project Proper_Traffic.circ as structural Verilog: 8 circuits, main circuit clk_2phase
module main (
);

  wire button_1_out, clk_2phase_1_phi_1, clk_2phase_1_phi_2, delta_1_q_prime_0, delta_1_q_prime_1,
       delta_1_q_prime_2, n3_bit_register_1_q_prime_0, n3_bit_register_1_q_prime_1,
       n3_bit_register_1_q_prime_2, n3_bit_register_2_q_prime_0, n3_bit_register_2_q_prime_1,
       n3_bit_register_2_q_prime_2, omega_1_a_a, omega_1_a_g, omega_1_a_r, omega_1_m_a, omega_1_m_g,
       omega_1_m_r;

  Button button_1 (.out(button_1_out));
  clk_2phase clk_2phase_1 (.phi_1(clk_2phase_1_phi_1), .phi_2(clk_2phase_1_phi_2));
  _3_bit_register u_3_bit_register_1 (
    .Q2(delta_1_q_prime_2), .Q1(delta_1_q_prime_1), .Q0(delta_1_q_prime_0),
    .Q_prime_2(n3_bit_register_1_q_prime_2), .Q_prime_1(n3_bit_register_1_q_prime_1),
    .Q_prime_0(n3_bit_register_1_q_prime_0), .en(clk_2phase_1_phi_2));
  _3_bit_register u_3_bit_register_2 (
    .Q2(n3_bit_register_1_q_prime_2), .Q1(n3_bit_register_1_q_prime_1), .Q0(n3_bit_register_1_q_prime_0),
    .Q_prime_2(n3_bit_register_2_q_prime_2), .Q_prime_1(n3_bit_register_2_q_prime_1),
    .Q_prime_0(n3_bit_register_2_q_prime_0), .en(clk_2phase_1_phi_1));
  delta delta_1 (
    .rst(button_1_out), .Q2(n3_bit_register_2_q_prime_2), .Q1(n3_bit_register_2_q_prime_1),
    .Q0(n3_bit_register_2_q_prime_0), .Q_prime_2(delta_1_q_prime_2), .Q_prime_1(delta_1_q_prime_1),
    .Q_prime_0(delta_1_q_prime_0));
  omega omega_1 (
    .Q2(n3_bit_register_2_q_prime_2), .Q1(n3_bit_register_2_q_prime_1), .Q0(n3_bit_register_2_q_prime_0),
    .M_G(omega_1_m_g), .M_A(omega_1_m_a), .M_R(omega_1_m_r), .A_G(omega_1_a_g), .A_A(omega_1_a_a),
    .A_R(omega_1_a_r));
  LED led_1 (.in(omega_1_m_g));
  LED led_2 (.in(omega_1_m_a));
  LED led_3 (.in(omega_1_m_r));
  LED led_4 (.in(omega_1_a_g));
  LED led_5 (.in(omega_1_a_a));
  LED led_6 (.in(omega_1_a_r));

  // Notes on the sheet:
  //   1
  //   2
  //   rst
  //   Q2
  //   Q1
  //   Q0
  //   Q2
  //   Q1
  //   Q0
endmodule

// CLK
module clk_2phase (
  output phi_1,
  output phi_2
);

  wire clock_1_out, nand_1_out, nand_2_out, not_1_out, not_2_out, not_3_out;

  Clock clock_1 (.out(clock_1_out));
  not not_1 (not_1_out, clock_1_out);
  not not_2 (not_2_out, nand_1_out);
  nand nand_1 (nand_1_out, not_1_out, phi_2);
  not not_3 (not_3_out, nand_2_out);
  nand nand_2 (nand_2_out, phi_1, clock_1_out);
  not not_4 (phi_1, not_2_out);
  not not_5 (phi_2, not_3_out);
endmodule

module DType (
  input  D,
  input  en,
  output Q,
  output Q_prime
);

  wire nand_1_out, nand_2_out, nand_3_out;

  not nand_1 (nand_1_out, D);  // NAND_Gate
  nand nand_2 (nand_2_out, D, en);
  nand nand_3 (nand_3_out, en, nand_1_out);
  nand nand_4 (Q, nand_2_out, Q_prime);
  nand nand_5 (Q_prime, Q, nand_3_out);
endmodule

// 3-bit reg
module _3_bit_register (
  input  Q2,
  input  Q1,
  input  Q0,
  input  en,
  output Q_prime_2,
  output Q_prime_1,
  output Q_prime_0
);

  DType dtype_1 (.D(Q2), .en(en), .Q(Q_prime_2));  // open: Q_prime
  DType dtype_2 (.D(Q1), .en(en), .Q(Q_prime_1));  // open: Q_prime
  DType dtype_3 (.D(Q0), .en(en), .Q(Q_prime_0));  // open: Q_prime
endmodule

// Delata
module delta (
  input  rst,
  input  Q2,
  input  Q1,
  input  Q0,
  output Q_prime_2,
  output Q_prime_1,
  output Q_prime_0
);

  wire and_1_out, and_2_out, and_3_out, and_4_out, not_1_out, not_2_out, not_3_out, not_4_out, not_5_out,
       not_6_out, not_7_out, not_8_out, not_9_out, not_10_out, not_11_out;

  not not_1 (not_1_out, Q1);
  and and_1 (and_1_out, not_1_out, not_2_out, Q2);
  not not_2 (not_2_out, rst);
  not not_3 (not_3_out, Q2);
  not not_4 (not_4_out, rst);
  and and_2 (and_2_out, not_3_out, not_4_out, Q1, Q0);
  not not_5 (not_5_out, rst);
  not not_6 (not_6_out, Q1);
  and and_3 (and_3_out, not_5_out, not_6_out, Q0);
  not not_7 (not_7_out, rst);
  not not_8 (not_8_out, Q2);
  and and_4 (and_4_out, not_7_out, not_8_out, not_9_out, Q1);
  not not_9 (not_9_out, Q0);
  not not_10 (not_10_out, rst);
  not not_11 (not_11_out, Q0);
  or or_1 (Q_prime_2, and_1_out, and_2_out);
  or or_2 (Q_prime_1, and_3_out, and_4_out);
  and and_5 (Q_prime_0, not_10_out, not_11_out);
endmodule

module omega (
  input  Q2,
  input  Q1,
  input  Q0,
  output M_G,
  output M_A,
  output M_R,
  output A_G,
  output A_A,
  output A_R
);

  wire and_3_out, and_4_out, and_5_out, and_7_out, and_8_out, and_9_out, and_10_out, not_1_out, not_2_out,
       not_3_out, not_4_out, not_5_out, not_6_out, not_7_out, not_8_out, not_9_out, not_10_out, not_11_out,
       not_12_out, not_13_out, not_14_out;

  not not_1 (not_1_out, Q1);
  not not_2 (not_2_out, Q2);
  not not_3 (not_3_out, Q0);
  not not_4 (not_4_out, Q0);
  not not_5 (not_5_out, Q1);
  not not_6 (not_6_out, Q1);
  not not_7 (not_7_out, Q2);
  not not_8 (not_8_out, Q0);
  not not_9 (not_9_out, Q1);
  not not_10 (not_10_out, Q2);
  not not_11 (not_11_out, Q1);
  not not_12 (not_12_out, Q1);
  not not_13 (not_13_out, Q2);
  not not_14 (not_14_out, Q0);
  and and_1 (M_G, Q0, not_1_out, not_2_out);
  and and_2 (M_A, not_3_out, Q1);
  and and_3 (and_3_out, not_4_out, not_5_out);
  and and_4 (and_4_out, not_6_out, Q2);
  and and_5 (and_5_out, Q0, Q1, not_7_out);
  and and_6 (A_G, not_8_out, not_9_out, Q2);
  and and_7 (and_7_out, Q0, Q1, not_10_out);
  and and_8 (and_8_out, Q0, not_11_out, Q2);
  and and_9 (and_9_out, not_12_out, not_13_out);
  and and_10 (and_10_out, not_14_out, Q1);
  or or_1 (M_R, and_3_out, and_4_out, and_5_out);
  or or_2 (A_A, and_7_out, and_8_out);
  or or_3 (A_R, and_9_out, and_10_out);
endmodule

module _3_bit_reg_1i_o (
  input  [2:0] in_1,
  input  en,
  output [2:0] out_3
);

  DType dtype_1 (.D(in_1[2]), .en(en), .Q(out_3[2]));  // open: Q_prime
  DType dtype_2 (.D(in_1[1]), .en(en), .Q(out_3[1]));  // open: Q_prime
  DType dtype_3 (.D(in_1[0]), .en(en), .Q(out_3[0]));  // open: Q_prime
endmodule

module new_main (
);

  wire button_1_out, clk_2phase_1_phi_1, clk_2phase_1_phi_2, delta_1_q_prime_0, delta_1_q_prime_1,
       delta_1_q_prime_2, n3_bit_reg_1i_o_1_p3, n3_bit_reg_1i_o_1_p4, n3_bit_reg_1i_o_1_p5,
       n3_bit_register_2_q_prime_0, n3_bit_register_2_q_prime_1, n3_bit_register_2_q_prime_2, omega_1_a_a,
       omega_1_a_g, omega_1_a_r, omega_1_m_a, omega_1_m_g, omega_1_m_r;
  wire [2:0] n3_bit_register_1_q_prime_0;

  Button button_1 (.out(button_1_out));
  clk_2phase clk_2phase_1 (.phi_1(clk_2phase_1_phi_1), .phi_2(clk_2phase_1_phi_2));
  _3_bit_register u_3_bit_register_1 (
    .Q2(delta_1_q_prime_2), .Q1(delta_1_q_prime_1), .Q0(delta_1_q_prime_0),
    .Q_prime_2(n3_bit_register_1_q_prime_0[2]), .Q_prime_1(n3_bit_register_1_q_prime_0[1]),
    .Q_prime_0(n3_bit_register_1_q_prime_0[0]), .en(clk_2phase_1_phi_2));
  _3_bit_register u_3_bit_register_2 (
    .Q2(n3_bit_register_1_q_prime_0[2]), .Q1(n3_bit_register_1_q_prime_0[1]),
    .Q0(n3_bit_register_1_q_prime_0[0]), .Q_prime_2(n3_bit_register_2_q_prime_2),
    .Q_prime_1(n3_bit_register_2_q_prime_1), .Q_prime_0(n3_bit_register_2_q_prime_0), .en(clk_2phase_1_phi_1));
  delta delta_1 (
    .rst(button_1_out), .Q2(n3_bit_register_2_q_prime_2), .Q1(n3_bit_register_2_q_prime_1),
    .Q0(n3_bit_register_2_q_prime_0), .Q_prime_2(delta_1_q_prime_2), .Q_prime_1(delta_1_q_prime_1),
    .Q_prime_0(delta_1_q_prime_0));
  // _3_bit_reg_1i_o 3_bit_reg_1i_o_1: pin names not known; wires that end beside it: n3_bit_register_1_q_prime_0, clk_2phase_1_phi_1, n3_bit_reg_1i_o_1_p3, n3_bit_reg_1i_o_1_p4, n3_bit_reg_1i_o_1_p5, n3_bit_reg_1i_o_1_p4, n3_bit_reg_1i_o_1_p5
  omega omega_1 (
    .Q2(n3_bit_register_2_q_prime_2), .Q1(n3_bit_register_2_q_prime_1), .Q0(n3_bit_register_2_q_prime_0),
    .M_G(omega_1_m_g), .M_A(omega_1_m_a), .M_R(omega_1_m_r), .A_G(omega_1_a_g), .A_A(omega_1_a_a),
    .A_R(omega_1_a_r));
  LED led_1 (.in(omega_1_m_g));
  LED led_2 (.in(omega_1_m_a));
  LED led_3 (.in(omega_1_m_r));
  LED led_4 (.in(omega_1_a_g));
  LED led_5 (.in(omega_1_a_a));
  LED led_6 (.in(omega_1_a_r));

  // Notes on the sheet:
  //   1
  //   2
  //   rst
  //   Q2
  //   Q1
  //   Q0
  //   Q2
  //   Q1
  //   Q0
endmodule
