// Logisim project fs_1.circ as structural Verilog: 1 circuit, main circuit main
module main (
  input  A,
  input  B,
  input  in_3
);

  wire and_1_out, and_2_out, and_3_out, and_4_out, clock_1_out, d_ff_1_q, d_ff_2_q, or_1_out, or_2_out,
       or_3_out, or_4_out;

  Clock clock_1 (.out(clock_1_out));
  or or_1 (or_1_out, B, A);
  or or_2 (or_2_out, in_3, A);
  D_Flip_Flop d_ff_1 (.D(or_1_out), .clk(clock_1_out), .Q(d_ff_1_q));  // open: Qn, preset, reset
  D_Flip_Flop d_ff_2 (.D(or_2_out), .clk(clock_1_out), .Q(d_ff_2_q));  // open: Qn, preset, reset
  and and_1 (and_1_out, B, d_ff_1_q);
  and and_2 (and_2_out, in_3, d_ff_2_q);
  and and_3 (and_3_out, A, d_ff_1_q);
  and and_4 (and_4_out, A, d_ff_2_q);
  or or_3 (or_3_out, and_1_out, and_3_out);
  or or_4 (or_4_out, and_2_out, and_4_out);
  LED led_1 (.in(or_3_out));
  LED led_2 (.in(or_4_out));
endmodule
