// Logisim project fsm_1_2_switch.circ as structural Verilog: 1 circuit, main circuit main
module main (
);

  wire and_1_out, and_2_out, button_1_out, button_2_out, clock_1_out, d_ff_1_q, or_1_out, or_2_out;

  Button button_1 (.out(button_1_out));
  Button button_2 (.out(button_2_out));
  or or_1 (or_1_out, button_2_out, button_1_out);
  Clock clock_1 (.out(clock_1_out));
  D_Flip_Flop d_ff_1 (.D(or_1_out), .clk(clock_1_out), .Q(d_ff_1_q));  // open: Qn, preset, reset
  and and_1 (and_1_out, button_2_out, d_ff_1_q);
  and and_2 (and_2_out, button_1_out, d_ff_1_q);
  or or_2 (or_2_out, and_1_out, and_2_out);
  LED led_1 (.in(or_2_out));

  // Notes on the sheet:
  //   A
  //   B
endmodule
